# Fritzing sketch ArduinoNano sketch2 (saved by Fritzing 0.9.4)
breadboards: 1

parts:
  Smart_LED_strip = NeoPixel Stick [part_number=1426]
  Vib_Motor_2-1_5V = Vibration Motor
  AC2DC_3_3V = generic-ac-power-supply [package=THT]
  Relay = Module 4 Relais 5V [package="Module 4 Relais 5V"]
  Part1 = Arduino Nano (Rev3.0)
  SP1 = SPEAKER [package=pcb_mount_speaker]
  Vib_Motor_2-2_3V = Vibration Motor
  Vib_Motor_1-2_3V = Vibration Motor
  Vib_Motor_1-1_3V = Vibration Motor
  SP2 = SPEAKER [package=pcb_mount_speaker]
  U4 = Molex Picoblade Series Header [part_number=0532610419 package=Picoblade-53261-0419]  # not connected
  AC2DC_5V = generic-ac-power-supply [package=THT]

nets:
  N1: Smart_LED_strip.DATAOUT, Part1.D2
  +5V: Smart_LED_strip.+5V, Relay.VCC, Part1.VIN, AC2DC_5V.pin4
  GND: Smart_LED_strip.GND, Relay.GND, Part1.GND, SP1.-, SP2.+, AC2DC_5V.pin3
  N2: Vib_Motor_2-1_5V.POS, Relay.K3-NO
  N3: Vib_Motor_2-1_5V.NEG, AC2DC_3_3V.pin4, Vib_Motor_2-2_3V.NEG, Vib_Motor_1-2_3V.NEG, Vib_Motor_1-1_3V.NEG
  N4: AC2DC_3_3V.pin3, Relay.K1-NF, Relay.K2-NF, Relay.K3-NF, Relay.K4-NF
  N5: Relay.IN1, Part1.D6
  N6: Relay.IN2, Part1.D5
  N7: Relay.IN3, Part1.D4
  N8: Relay.IN4, Part1.D3
  N9: Relay.K1-NO, Vib_Motor_1-1_3V.POS
  N10: Relay.K2-NO, Vib_Motor_1-2_3V.POS
  N11: Relay.K4-NO, Vib_Motor_2-2_3V.POS
  N12: Part1.D10, SP1.+
  N13: Part1.D12/MISO, SP2.-

custom parts:
  NeoPixel Stick: Make your own little LED strip arrangement with this stick of NeoPixel LEDs. We crammed 8 of the tiny 5050 (5mm x 5mm) smart RGB LEDs onto a PCB with mounting holes and a chainable design. Use only one microcontroller pin to control as many as you can chain together! Each LED is addressable as the driver chip is inside the LED. Each one has ~18mA constant current drive so the color will be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
  Vibration Motor: An eccentric vibration motor!
  generic-ac-power-supply: Generic ac power supply module. Use as is, or customize the svgs to fit your particular device (as they are all different.) Provides AC input and single DC output. This is variant 2, with pcb modified to match the url for a specific device.
  Module 4 Relais 5V: Module 4 Relais 5V 4x SPD-06VDC-SD-C
